# Fritzing sketch HID-Joystick (saved by Fritzing 0.9.6b)
breadboards: 1

parts:
  Bauteil1 = Arduino Pro Micro (Clone)
  S2 = Pushbutton [package="[THT]"]
  S3 = Pushbutton [package="[THT]"]
  Bauteil2 = Thumb Joystick
  R1 = Resistor [tolerance=±5% power=0.25 resistance=10k package=THT]
  R2 = Resistor [tolerance=±5% power=0.25 resistance=10k package=THT]
  R3 = Resistor [tolerance=±5% power=0.25 resistance=10k package=THT]

nets:
  GND: Bauteil1.GND, Bauteil2.GND, R1.Pin_1, R2.Pin_1, R3.Pin_0
  N1: Bauteil1.D2, S2.Pin_1, S2.Pin_2, R1.Pin_0
  N2: Bauteil1.D3, S3.Pin_1, S3.Pin_2, R2.Pin_0
  N3: Bauteil1.D4, Bauteil2.SEL, R3.Pin_1
  N4: Bauteil1.A0, Bauteil2.HORZ
  N5: Bauteil1.A1, Bauteil2.VERT
  VCC: Bauteil1.VCC, S2.Pin_3, S2.Pin_4, S3.Pin_3, S3.Pin_4, Bauteil2.VCC
